// Logisim project cpu.circ as structural Verilog: 13 circuits, main circuit main
module main (
  input  reset
);

  wire ALUinB, and_2_out, and_3_out, and_4_out, and_5_out, and_6_out, beq, bgt, clk, j, jal, jr, mem,
       memorysubcircuit_1_oe_latched, memorysubcircuit_1_we_latched, not_1_out, not_2_out, not_3_out,
       not_4_out, not_5_out, not_6_out, not_7_out, not_8_out, not_9_out, not_10_out, not_11_out, not_12_out,
       not_13_out, not_14_out, or_1_out, or_2_out, positive, rdrs2, rwe, sw_out, valid, zero;
  wire [1:0] ALUorDMorinputorNextPC, jump;
  wire [2:0] alucontrol_1_aluop, multiplexer_1_out, multiplexer_2_out;
  wire [3:0] opcode, upper4;
  wire [6:0] keyboard_1_data, registerfile_1_rs1content;
  wire [11:0] address, reg_1_data_out;
  wire [15:0] add_1_registerdest, add_2_registerdest, compare, controlled_buffer_1_out,
       Data_Memory_55253221_dout, memorysubcircuit_1_address_latched, memorysubcircuit_1_data_in_latched,
       multiplexer_3_out, multiplexer_4_out, multiplexer_5_out, multiplexer_6_out, multiplexer_7_out, newimm,
       registerfile_1_rs2content;
  wire [15:7] registerfile_1_rs1content_2;

  selectors selectors_1 (
    .opcode(opcode), .ALUorDMorinputorNextPC(ALUorDMorinputorNextPC), .ALUinB(ALUinB), .rdrs2(rdrs2),
    .rwe(rwe), .beq(beq), .bgt(bgt), .jal(jal), .jr(jr), .j(j), .memory(mem));
  signextender signextender_1 (.imm(address[5:0]), .newimm(newimm));
  \reg  reg_1 (.data_in(multiplexer_6_out), .clk(clk), .we(1'b1), .reset(reset), .data_out({upper4, reg_1_data_out}));
  add add_1 (
    .registersource1(16'h1), .registersource2({upper4, reg_1_data_out}), .registerdest(add_1_registerdest));  // open: ovf
  ROM #(.addrWidth(16), .dataWidth(16)) Instruction_Memory (.addr({upper4, reg_1_data_out}), .data({opcode, address}));
  Clock clock_1 (.out(clk));
  not not_1 (not_1_out, compare[15]);
  add add_2 (
    .registersource1(add_1_registerdest), .registersource2(newimm), .registerdest(add_2_registerdest));  // open: ovf
  nor nor_1 (zero, compare[0], compare[1], compare[2], compare[3], compare[4], compare[5], compare[6], compare[7], compare[8], compare[9], compare[10], compare[11], compare[12], compare[13], compare[14], compare[15]);
  not not_2 (not_2_out, zero);
  Multiplexer #(.width(3), .enable("false")) multiplexer_1 (
    .in0(multiplexer_2_out), .in1(3'b111), .out(multiplexer_1_out), .sel(jal));
  and and_1 (positive, not_1_out, not_2_out);
  Multiplexer #(.width(3), .enable("false")) multiplexer_2 (
    .in0(address[5:3]), .in1(address[8:6]), .out(multiplexer_2_out), .sel(rdrs2));
  Multiplexer #(.select(2), .width(16), .enable("false")) multiplexer_3 (
    .in0(compare), .in1(Data_Memory_55253221_dout), .in2(multiplexer_7_out), .in3(add_1_registerdest),
    .out(multiplexer_3_out), .sel(ALUorDMorinputorNextPC));
  not not_3 (not_3_out, clk);
  RegisterFile registerfile_1 (
    .registerdest(multiplexer_1_out), .data_in(multiplexer_3_out), .clk(not_3_out), .reset(reset),
    .we_writeregister(rwe), .rs1(address[11:9]), .rs2(address[8:6]),
    .rs1content({registerfile_1_rs1content_2, registerfile_1_rs1content}),
    .rs2content(registerfile_1_rs2content));
  not not_4 (not_4_out, jr);
  not not_5 (not_5_out, or_1_out);
  not not_6 (not_6_out, opcode[3]);
  Multiplexer #(.width(16), .enable("false")) multiplexer_4 (
    .in0(registerfile_1_rs2content), .in1(newimm), .out(multiplexer_4_out), .sel(ALUinB));
  and and_2 (and_2_out, not_4_out, not_5_out);
  or or_1 (or_1_out, j, jal);
  not not_7 (not_7_out, opcode[2]);
  assign controlled_buffer_1_out = mem ? registerfile_1_rs2content : 16'bz;  // Controlled_Buffer controlled_buffer_1
  ALU alu_1 (
    .registersource1({registerfile_1_rs1content_2, registerfile_1_rs1content}),
    .registersource2(multiplexer_4_out), .shamt(address[2:0]), .registerdest(compare),
    .ALUop(alucontrol_1_aluop));
  ALUcontrol alucontrol_1 (.opcode(opcode), .ALUop(alucontrol_1_aluop));
  assign jump = and_2_out ? 2'b00 : 2'bz;  // Controlled_Buffer controlled_buffer_2
  assign jump = or_1_out ? 2'b01 : 2'bz;  // Controlled_Buffer controlled_buffer_3
  assign jump = jr ? 2'b10 : 2'bz;  // Controlled_Buffer controlled_buffer_4
  and and_3 (and_3_out, beq, zero);
  and and_4 (and_4_out, bgt, positive);
  and sw (sw_out, opcode[0], opcode[1], not_7_out, not_6_out);
  memorysubcircuit memorysubcircuit_1 (
    .address(compare), .WE(sw_out), .clk(clk), .data_in(controlled_buffer_1_out),
    .address_latched(memorysubcircuit_1_address_latched), .WE_latched(memorysubcircuit_1_we_latched),
    .OE_latched(memorysubcircuit_1_oe_latched), .data_in_latched(memorysubcircuit_1_data_in_latched));
  or or_2 (or_2_out, and_3_out, and_4_out);
  RAM #(.addrWidth(16), .dataWidth(16), .trigger("high"), .databus("bibus")) Data_Memory_55253221 (
    .addr(memorysubcircuit_1_address_latched), .we(memorysubcircuit_1_we_latched),
    .oe(memorysubcircuit_1_oe_latched), .din(memorysubcircuit_1_data_in_latched),
    .dout(Data_Memory_55253221_dout));
  Multiplexer #(.width(16), .enable("false")) multiplexer_5 (
    .in0(add_1_registerdest), .in1(add_2_registerdest), .out(multiplexer_5_out), .sel(or_2_out));
  not not_8 (not_8_out, opcode[0]);
  Keyboard keyboard_1 (.clk(clk), .re(and_6_out), .clr(reset), .avail(valid), .data(keyboard_1_data));
  not not_9 (not_9_out, opcode[1]);
  not not_10 (not_10_out, opcode[2]);
  not not_11 (not_11_out, opcode[3]);
  and and_5 (and_5_out, not_8_out, not_9_out, not_10_out, not_11_out);
  not not_12 (not_12_out, opcode[1]);
  not not_13 (not_13_out, opcode[2]);
  not not_14 (not_14_out, opcode[3]);
  Multiplexer #(.select(2), .width(16), .enable("false")) multiplexer_6 (
    .in0(multiplexer_5_out), .in1({upper4, address}),
    .in2({registerfile_1_rs1content_2, registerfile_1_rs1content}), .out(multiplexer_6_out), .sel(jump));  // open: in3
  TTY #(.rows(13), .cols(80), .trigger("falling")) tty_1 (
    .data(registerfile_1_rs1content), .clk(clk), .we(and_5_out), .clr(reset));
  and and_6 (and_6_out, opcode[0], not_12_out, not_13_out, not_14_out);
  Multiplexer #(.width(16), .enable("false")) multiplexer_7 (
    .in0(16'h80), .in1({{9{1'b0}}, keyboard_1_data}), .out(multiplexer_7_out), .sel(valid));

  // Other names for the same wires on the sheet: imm[5:0] = address[5:0]; rd[2:0] = address[5:3];
  //   rs1[2:0] = address[11:9]; rs2[2:0] = address[8:6]; shamt[2:0] = address[2:0]
endmodule

module ALU (
  input  [15:0] registersource1,
  input  [15:0] registersource2,
  input  [2:0] ALUop,
  input  [2:0] shamt,
  output [15:0] registerdest
);

  wire [15:0] add_1_registerdest, and_1_out, or_1_out, shl_1_registerdest, shra_1_registerdest,
       sub_1_registerdest;

  sub sub_1 (
    .registersource1(registersource1), .registersource2(registersource2), .registerdest(sub_1_registerdest));  // open: ovf
  shra shra_1 (.shamt(shamt), .registersource1(registersource1), .registerdest(shra_1_registerdest));
  shl shl_1 (.shamt(shamt), .registersource1(registersource1), .registerdest(shl_1_registerdest));
  assign or_1_out = registersource1 | registersource2;  // OR_Gate or_1, 16 bits wide
  assign and_1_out = registersource1 & registersource2;  // AND_Gate and_1, 16 bits wide
  add add_1 (
    .registersource1(registersource1), .registersource2(registersource2), .registerdest(add_1_registerdest));  // open: ovf
  Multiplexer #(.select(3), .width(16), .enable("false")) multiplexer_1 (
    .in0(or_1_out), .in1(and_1_out), .in2(add_1_registerdest), .in3(sub_1_registerdest),
    .in4(shra_1_registerdest), .in5(shl_1_registerdest), .in6({16{1'b0}}), .in7({16{1'b0}}),
    .out(registerdest), .sel(ALUop));
endmodule

module add (
  input  [15:0] registersource1,
  input  [15:0] registersource2,
  output ovf,
  output [15:0] registerdest
);

  wire addsubcircuit_1_cout, addsubcircuit_3_cout, addsubcircuit_5_cout, addsubcircuit_6_cout,
       addsubcircuit_7_cout, addsubcircuit_8_cout, addsubcircuit_9_cout, addsubcircuit_10_cout,
       addsubcircuit_11_cout, addsubcircuit_12_cout, addsubcircuit_13_cout, addsubcircuit_14_cout,
       addsubcircuit_15_cout, addsubcircuit_16_cout, addsubcircuit_17_cout, addsubcircuit_18_cout, xor_2_out,
       xor_3_out, xor_4_out, xor_5_out, xor_6_out, xor_7_out, xor_8_out, xor_9_out, xor_10_out, xor_11_out,
       xor_12_out, xor_13_out, xor_14_out, xor_15_out, xor_16_out, xor_17_out;

  addsubcircuit addsubcircuit_1 (
    .Cin(addsubcircuit_3_cout), .a(xor_2_out), .b(registersource1[15]), .sum(registerdest[15]),
    .Cout(addsubcircuit_1_cout));
  addsubcircuit addsubcircuit_2 (
    .Cin(addsubcircuit_3_cout), .a(xor_2_out), .b(registersource1[15]), .sum(registerdest[15]),
    .Cout(addsubcircuit_1_cout));
  addsubcircuit addsubcircuit_3 (
    .Cin(addsubcircuit_5_cout), .a(xor_3_out), .b(registersource1[14]), .sum(registerdest[14]),
    .Cout(addsubcircuit_3_cout));
  addsubcircuit addsubcircuit_4 (
    .Cin(addsubcircuit_5_cout), .a(xor_3_out), .b(registersource1[14]), .sum(registerdest[14]),
    .Cout(addsubcircuit_3_cout));
  xor xor_1 (ovf, addsubcircuit_1_cout, addsubcircuit_3_cout);
  xor xor_2 (xor_2_out, 1'b0, registersource2[15]);
  addsubcircuit addsubcircuit_5 (
    .Cin(addsubcircuit_6_cout), .a(xor_4_out), .b(registersource1[13]), .sum(registerdest[13]),
    .Cout(addsubcircuit_5_cout));
  xor xor_3 (xor_3_out, 1'b0, registersource2[14]);
  addsubcircuit addsubcircuit_6 (
    .Cin(addsubcircuit_7_cout), .a(xor_5_out), .b(registersource1[12]), .sum(registerdest[12]),
    .Cout(addsubcircuit_6_cout));
  xor xor_4 (xor_4_out, 1'b0, registersource2[13]);
  addsubcircuit addsubcircuit_7 (
    .Cin(addsubcircuit_8_cout), .a(xor_6_out), .b(registersource1[11]), .sum(registerdest[11]),
    .Cout(addsubcircuit_7_cout));
  xor xor_5 (xor_5_out, 1'b0, registersource2[12]);
  addsubcircuit addsubcircuit_8 (
    .Cin(addsubcircuit_9_cout), .a(xor_7_out), .b(registersource1[10]), .sum(registerdest[10]),
    .Cout(addsubcircuit_8_cout));
  xor xor_6 (xor_6_out, 1'b0, registersource2[11]);
  addsubcircuit addsubcircuit_9 (
    .Cin(addsubcircuit_10_cout), .a(xor_8_out), .b(registersource1[9]), .sum(registerdest[9]),
    .Cout(addsubcircuit_9_cout));
  xor xor_7 (xor_7_out, 1'b0, registersource2[10]);
  addsubcircuit addsubcircuit_10 (
    .Cin(addsubcircuit_11_cout), .a(xor_9_out), .b(registersource1[8]), .sum(registerdest[8]),
    .Cout(addsubcircuit_10_cout));
  xor xor_8 (xor_8_out, 1'b0, registersource2[9]);
  addsubcircuit addsubcircuit_11 (
    .Cin(addsubcircuit_12_cout), .a(xor_10_out), .b(registersource1[7]), .sum(registerdest[7]),
    .Cout(addsubcircuit_11_cout));
  xor xor_9 (xor_9_out, 1'b0, registersource2[8]);
  addsubcircuit addsubcircuit_12 (
    .Cin(addsubcircuit_13_cout), .a(xor_11_out), .b(registersource1[6]), .sum(registerdest[6]),
    .Cout(addsubcircuit_12_cout));
  xor xor_10 (xor_10_out, 1'b0, registersource2[7]);
  addsubcircuit addsubcircuit_13 (
    .Cin(addsubcircuit_14_cout), .a(xor_12_out), .b(registersource1[5]), .sum(registerdest[5]),
    .Cout(addsubcircuit_13_cout));
  xor xor_11 (xor_11_out, 1'b0, registersource2[6]);
  addsubcircuit addsubcircuit_14 (
    .Cin(addsubcircuit_15_cout), .a(xor_13_out), .b(registersource1[4]), .sum(registerdest[4]),
    .Cout(addsubcircuit_14_cout));
  xor xor_12 (xor_12_out, 1'b0, registersource2[5]);
  addsubcircuit addsubcircuit_15 (
    .Cin(addsubcircuit_16_cout), .a(xor_14_out), .b(registersource1[3]), .sum(registerdest[3]),
    .Cout(addsubcircuit_15_cout));
  xor xor_13 (xor_13_out, 1'b0, registersource2[4]);
  addsubcircuit addsubcircuit_16 (
    .Cin(addsubcircuit_17_cout), .a(xor_15_out), .b(registersource1[2]), .sum(registerdest[2]),
    .Cout(addsubcircuit_16_cout));
  xor xor_14 (xor_14_out, 1'b0, registersource2[3]);
  addsubcircuit addsubcircuit_17 (
    .Cin(addsubcircuit_18_cout), .a(xor_16_out), .b(registersource1[1]), .sum(registerdest[1]),
    .Cout(addsubcircuit_17_cout));
  xor xor_15 (xor_15_out, 1'b0, registersource2[2]);
  addsubcircuit addsubcircuit_18 (
    .Cin(1'b0), .a(xor_17_out), .b(registersource1[0]), .sum(registerdest[0]), .Cout(addsubcircuit_18_cout));
  xor xor_16 (xor_16_out, 1'b0, registersource2[1]);
  xor xor_17 (xor_17_out, 1'b0, registersource2[0]);

  // Other names for the same wires on the sheet: s1 = registerdest[0]; s2 = registerdest[1]; s3 = registerdest[2];
  //   s4 = registerdest[3]; s5 = registerdest[4]; s6 = registerdest[5]; s7 = registerdest[6]; s8 = registerdest[7];
  //   s9 = registerdest[8]; s10 = registerdest[9]; s11 = registerdest[10]; s12 = registerdest[11];
  //   s13 = registerdest[12]; s14 = registerdest[13]; s15 = registerdest[14]; s16 = registerdest[15];
  //   a1 = registersource1[0]; a2 = registersource1[1]; a3 = registersource1[2]; a4 = registersource1[3];
  //   a5 = registersource1[4]; a6 = registersource1[5]; a7 = registersource1[6]; a8 = registersource1[7];
  //   a9 = registersource1[8]; a10 = registersource1[9]; a11 = registersource1[10]; a12 = registersource1[11];
  //   a13 = registersource1[12]; a14 = registersource1[13]; a15 = registersource1[14]; a16 = registersource1[15];
  //   b1 = registersource2[0]; b2 = registersource2[1]; b3 = registersource2[2]; b4 = registersource2[3];
  //   b5 = registersource2[4]; b6 = registersource2[5]; b7 = registersource2[6]; b8 = registersource2[7];
  //   b9 = registersource2[8]; b10 = registersource2[9]; b11 = registersource2[10]; b12 = registersource2[11];
  //   b13 = registersource2[12]; b14 = registersource2[13]; b15 = registersource2[14]; b16 = registersource2[15]
endmodule

module sub (
  input  [15:0] registersource1,
  input  [15:0] registersource2,
  output ovf,
  output [15:0] registerdest
);

  wire addsubcircuit_1_cout, addsubcircuit_4_cout, addsubcircuit_6_cout, addsubcircuit_7_cout,
       addsubcircuit_8_cout, addsubcircuit_9_cout, addsubcircuit_10_cout, addsubcircuit_11_cout,
       addsubcircuit_12_cout, addsubcircuit_13_cout, addsubcircuit_14_cout, addsubcircuit_15_cout,
       addsubcircuit_16_cout, addsubcircuit_17_cout, addsubcircuit_18_cout, addsubcircuit_19_cout, xor_2_out,
       xor_3_out, xor_4_out, xor_5_out, xor_6_out, xor_7_out, xor_8_out, xor_9_out, xor_10_out, xor_11_out,
       xor_12_out, xor_13_out, xor_14_out, xor_15_out, xor_16_out, xor_17_out;

  addsubcircuit addsubcircuit_1 (
    .Cin(addsubcircuit_4_cout), .a(xor_2_out), .b(registersource1[15]), .sum(registerdest[15]),
    .Cout(addsubcircuit_1_cout));
  addsubcircuit addsubcircuit_2 (
    .Cin(addsubcircuit_4_cout), .a(xor_2_out), .b(registersource1[15]), .sum(registerdest[15]),
    .Cout(addsubcircuit_1_cout));
  addsubcircuit addsubcircuit_3 ();  // open: Cin, a, b, sum, Cout
  addsubcircuit addsubcircuit_4 (
    .Cin(addsubcircuit_6_cout), .a(xor_3_out), .b(registersource1[14]), .sum(registerdest[14]),
    .Cout(addsubcircuit_4_cout));
  addsubcircuit addsubcircuit_5 (
    .Cin(addsubcircuit_6_cout), .a(xor_3_out), .b(registersource1[14]), .sum(registerdest[14]),
    .Cout(addsubcircuit_4_cout));
  xor xor_1 (ovf, addsubcircuit_1_cout, addsubcircuit_4_cout);
  xor xor_2 (xor_2_out, 1'b1, registersource2[15]);
  addsubcircuit addsubcircuit_6 (
    .Cin(addsubcircuit_7_cout), .a(xor_4_out), .b(registersource1[13]), .sum(registerdest[13]),
    .Cout(addsubcircuit_6_cout));
  xor xor_3 (xor_3_out, 1'b1, registersource2[14]);
  addsubcircuit addsubcircuit_7 (
    .Cin(addsubcircuit_8_cout), .a(xor_5_out), .b(registersource1[12]), .sum(registerdest[12]),
    .Cout(addsubcircuit_7_cout));
  xor xor_4 (xor_4_out, 1'b1, registersource2[13]);
  addsubcircuit addsubcircuit_8 (
    .Cin(addsubcircuit_9_cout), .a(xor_6_out), .b(registersource1[11]), .sum(registerdest[11]),
    .Cout(addsubcircuit_8_cout));
  xor xor_5 (xor_5_out, 1'b1, registersource2[12]);
  addsubcircuit addsubcircuit_9 (
    .Cin(addsubcircuit_10_cout), .a(xor_7_out), .b(registersource1[10]), .sum(registerdest[10]),
    .Cout(addsubcircuit_9_cout));
  xor xor_6 (xor_6_out, 1'b1, registersource2[11]);
  addsubcircuit addsubcircuit_10 (
    .Cin(addsubcircuit_11_cout), .a(xor_8_out), .b(registersource1[9]), .sum(registerdest[9]),
    .Cout(addsubcircuit_10_cout));
  xor xor_7 (xor_7_out, 1'b1, registersource2[10]);
  addsubcircuit addsubcircuit_11 (
    .Cin(addsubcircuit_12_cout), .a(xor_9_out), .b(registersource1[8]), .sum(registerdest[8]),
    .Cout(addsubcircuit_11_cout));
  xor xor_8 (xor_8_out, 1'b1, registersource2[9]);
  addsubcircuit addsubcircuit_12 (
    .Cin(addsubcircuit_13_cout), .a(xor_10_out), .b(registersource1[7]), .sum(registerdest[7]),
    .Cout(addsubcircuit_12_cout));
  xor xor_9 (xor_9_out, 1'b1, registersource2[8]);
  addsubcircuit addsubcircuit_13 (
    .Cin(addsubcircuit_14_cout), .a(xor_11_out), .b(registersource1[6]), .sum(registerdest[6]),
    .Cout(addsubcircuit_13_cout));
  xor xor_10 (xor_10_out, 1'b1, registersource2[7]);
  addsubcircuit addsubcircuit_14 (
    .Cin(addsubcircuit_15_cout), .a(xor_12_out), .b(registersource1[5]), .sum(registerdest[5]),
    .Cout(addsubcircuit_14_cout));
  xor xor_11 (xor_11_out, 1'b1, registersource2[6]);
  addsubcircuit addsubcircuit_15 (
    .Cin(addsubcircuit_16_cout), .a(xor_13_out), .b(registersource1[4]), .sum(registerdest[4]),
    .Cout(addsubcircuit_15_cout));
  xor xor_12 (xor_12_out, 1'b1, registersource2[5]);
  addsubcircuit addsubcircuit_16 (
    .Cin(addsubcircuit_17_cout), .a(xor_14_out), .b(registersource1[3]), .sum(registerdest[3]),
    .Cout(addsubcircuit_16_cout));
  xor xor_13 (xor_13_out, 1'b1, registersource2[4]);
  addsubcircuit addsubcircuit_17 (
    .Cin(addsubcircuit_18_cout), .a(xor_15_out), .b(registersource1[2]), .sum(registerdest[2]),
    .Cout(addsubcircuit_17_cout));
  xor xor_14 (xor_14_out, 1'b1, registersource2[3]);
  addsubcircuit addsubcircuit_18 (
    .Cin(addsubcircuit_19_cout), .a(xor_16_out), .b(registersource1[1]), .sum(registerdest[1]),
    .Cout(addsubcircuit_18_cout));
  xor xor_15 (xor_15_out, 1'b1, registersource2[2]);
  addsubcircuit addsubcircuit_19 (
    .Cin(1'b1), .a(xor_17_out), .b(registersource1[0]), .sum(registerdest[0]), .Cout(addsubcircuit_19_cout));
  xor xor_16 (xor_16_out, 1'b1, registersource2[1]);
  xor xor_17 (xor_17_out, 1'b1, registersource2[0]);

  // Other names for the same wires on the sheet: s1 = registerdest[0]; s2 = registerdest[1]; s3 = registerdest[2];
  //   s4 = registerdest[3]; s5 = registerdest[4]; s6 = registerdest[5]; s7 = registerdest[6]; s8 = registerdest[7];
  //   s9 = registerdest[8]; s10 = registerdest[9]; s11 = registerdest[10]; s12 = registerdest[11];
  //   s13 = registerdest[12]; s14 = registerdest[13]; s15 = registerdest[14]; s16 = registerdest[15];
  //   a1 = registersource1[0]; a2 = registersource1[1]; a3 = registersource1[2]; a4 = registersource1[3];
  //   a5 = registersource1[4]; a6 = registersource1[5]; a7 = registersource1[6]; a8 = registersource1[7];
  //   a9 = registersource1[8]; a10 = registersource1[9]; a11 = registersource1[10]; a12 = registersource1[11];
  //   a13 = registersource1[12]; a14 = registersource1[13]; a15 = registersource1[14]; a16 = registersource1[15];
  //   b1 = registersource2[0]; b2 = registersource2[1]; b3 = registersource2[2]; b4 = registersource2[3];
  //   b5 = registersource2[4]; b6 = registersource2[5]; b7 = registersource2[6]; b8 = registersource2[7];
  //   b9 = registersource2[8]; b10 = registersource2[9]; b11 = registersource2[10]; b12 = registersource2[11];
  //   b13 = registersource2[12]; b14 = registersource2[13]; b15 = registersource2[14]; b16 = registersource2[15]
endmodule

module addsubcircuit (
  input  Cin,
  input  a,
  input  b,
  output sum,
  output Cout
);

  wire and_1_out, and_2_out, xor_1_out;

  and and_1 (and_1_out, b, a);
  xor xor_1 (xor_1_out, a, b);
  or or_1 (Cout, and_1_out, and_2_out);
  and and_2 (and_2_out, xor_1_out, Cin);
  xor xor_2 (sum, Cin, xor_1_out);
endmodule

module shl (
  input  [2:0] shamt,
  input  [15:0] registersource1,
  output [15:0] registerdest
);

  wire multiplexer_1_out, multiplexer_2_out, multiplexer_3_out, multiplexer_4_out, multiplexer_5_out,
       multiplexer_6_out, multiplexer_7_out, multiplexer_8_out, multiplexer_9_out, multiplexer_10_out,
       multiplexer_11_out, multiplexer_12_out, multiplexer_13_out, multiplexer_14_out, multiplexer_15_out,
       multiplexer_16_out, multiplexer_17_out, multiplexer_18_out, multiplexer_19_out, multiplexer_20_out,
       multiplexer_21_out, multiplexer_22_out, multiplexer_23_out, multiplexer_24_out, multiplexer_25_out,
       multiplexer_26_out, multiplexer_27_out, multiplexer_28_out, multiplexer_29_out, multiplexer_30_out,
       multiplexer_31_out, multiplexer_32_out;

  Multiplexer #(.enable("false")) multiplexer_1 (
    .in0(registersource1[0]), .in1(1'b0), .out(multiplexer_1_out), .sel(shamt[0]));
  Multiplexer #(.enable("false")) multiplexer_2 (
    .in0(registersource1[1]), .in1(registersource1[0]), .out(multiplexer_2_out), .sel(shamt[0]));
  Multiplexer #(.enable("false")) multiplexer_3 (
    .in0(registersource1[2]), .in1(registersource1[1]), .out(multiplexer_3_out), .sel(shamt[0]));
  Multiplexer #(.enable("false")) multiplexer_4 (
    .in0(registersource1[3]), .in1(registersource1[2]), .out(multiplexer_4_out), .sel(shamt[0]));
  Multiplexer #(.enable("false")) multiplexer_5 (
    .in0(registersource1[4]), .in1(registersource1[3]), .out(multiplexer_5_out), .sel(shamt[0]));
  Multiplexer #(.enable("false")) multiplexer_6 (
    .in0(registersource1[5]), .in1(registersource1[4]), .out(multiplexer_6_out), .sel(shamt[0]));
  Multiplexer #(.enable("false")) multiplexer_7 (
    .in0(registersource1[6]), .in1(registersource1[5]), .out(multiplexer_7_out), .sel(shamt[0]));
  Multiplexer #(.enable("false")) multiplexer_8 (
    .in0(registersource1[7]), .in1(registersource1[6]), .out(multiplexer_8_out), .sel(shamt[0]));
  Multiplexer #(.enable("false")) multiplexer_9 (
    .in0(registersource1[8]), .in1(registersource1[7]), .out(multiplexer_9_out), .sel(shamt[0]));
  Multiplexer #(.enable("false")) multiplexer_10 (
    .in0(registersource1[9]), .in1(registersource1[8]), .out(multiplexer_10_out), .sel(shamt[0]));
  Multiplexer #(.enable("false")) multiplexer_11 (
    .in0(registersource1[10]), .in1(registersource1[9]), .out(multiplexer_11_out), .sel(shamt[0]));
  Multiplexer #(.enable("false")) multiplexer_12 (
    .in0(registersource1[11]), .in1(registersource1[10]), .out(multiplexer_12_out), .sel(shamt[0]));
  Multiplexer #(.enable("false")) multiplexer_13 (
    .in0(registersource1[12]), .in1(registersource1[11]), .out(multiplexer_13_out), .sel(shamt[0]));
  Multiplexer #(.enable("false")) multiplexer_14 (
    .in0(registersource1[13]), .in1(registersource1[12]), .out(multiplexer_14_out), .sel(shamt[0]));
  Multiplexer #(.enable("false")) multiplexer_15 (
    .in0(registersource1[14]), .in1(registersource1[13]), .out(multiplexer_15_out), .sel(shamt[0]));
  Multiplexer #(.enable("false")) multiplexer_16 (
    .in0(registersource1[15]), .in1(registersource1[14]), .out(multiplexer_16_out), .sel(shamt[0]));
  Multiplexer #(.enable("false")) multiplexer_17 (
    .in0(multiplexer_15_out), .in1(multiplexer_13_out), .out(multiplexer_17_out), .sel(shamt[1]));
  Multiplexer #(.enable("false")) multiplexer_18 (
    .in0(multiplexer_16_out), .in1(multiplexer_14_out), .out(multiplexer_18_out), .sel(shamt[1]));
  Multiplexer #(.enable("false")) multiplexer_19 (
    .in0(multiplexer_9_out), .in1(multiplexer_7_out), .out(multiplexer_19_out), .sel(shamt[1]));
  Multiplexer #(.enable("false")) multiplexer_20 (
    .in0(multiplexer_10_out), .in1(multiplexer_8_out), .out(multiplexer_20_out), .sel(shamt[1]));
  Multiplexer #(.enable("false")) multiplexer_21 (
    .in0(multiplexer_11_out), .in1(multiplexer_9_out), .out(multiplexer_21_out), .sel(shamt[1]));
  Multiplexer #(.enable("false")) multiplexer_22 (
    .in0(multiplexer_12_out), .in1(multiplexer_10_out), .out(multiplexer_22_out), .sel(shamt[1]));
  Multiplexer #(.enable("false")) multiplexer_23 (
    .in0(multiplexer_13_out), .in1(multiplexer_11_out), .out(multiplexer_23_out), .sel(shamt[1]));
  Multiplexer #(.enable("false")) multiplexer_24 (
    .in0(multiplexer_14_out), .in1(multiplexer_12_out), .out(multiplexer_24_out), .sel(shamt[1]));
  Multiplexer #(.enable("false")) multiplexer_25 (
    .in0(multiplexer_3_out), .in1(multiplexer_1_out), .out(multiplexer_25_out), .sel(shamt[1]));
  Multiplexer #(.enable("false")) multiplexer_26 (
    .in0(multiplexer_4_out), .in1(multiplexer_2_out), .out(multiplexer_26_out), .sel(shamt[1]));
  Multiplexer #(.enable("false")) multiplexer_27 (
    .in0(multiplexer_5_out), .in1(multiplexer_3_out), .out(multiplexer_27_out), .sel(shamt[1]));
  Multiplexer #(.enable("false")) multiplexer_28 (
    .in0(multiplexer_6_out), .in1(multiplexer_4_out), .out(multiplexer_28_out), .sel(shamt[1]));
  Multiplexer #(.enable("false")) multiplexer_29 (
    .in0(multiplexer_7_out), .in1(multiplexer_5_out), .out(multiplexer_29_out), .sel(shamt[1]));
  Multiplexer #(.enable("false")) multiplexer_30 (
    .in0(multiplexer_8_out), .in1(multiplexer_6_out), .out(multiplexer_30_out), .sel(shamt[1]));
  Multiplexer #(.enable("false")) multiplexer_31 (
    .in0(multiplexer_1_out), .in1(1'b0), .out(multiplexer_31_out), .sel(shamt[1]));
  Multiplexer #(.enable("false")) multiplexer_32 (
    .in0(multiplexer_2_out), .in1(1'b0), .out(multiplexer_32_out), .sel(shamt[1]));
  Multiplexer #(.enable("false")) multiplexer_33 (
    .in0(multiplexer_18_out), .in1(multiplexer_22_out), .out(registerdest[15]), .sel(shamt[2]));
  Multiplexer #(.enable("false")) multiplexer_34 (
    .in0(multiplexer_23_out), .in1(multiplexer_19_out), .out(registerdest[12]), .sel(shamt[2]));
  Multiplexer #(.enable("false")) multiplexer_35 (
    .in0(multiplexer_24_out), .in1(multiplexer_20_out), .out(registerdest[13]), .sel(shamt[2]));
  Multiplexer #(.enable("false")) multiplexer_36 (
    .in0(multiplexer_17_out), .in1(multiplexer_21_out), .out(registerdest[14]), .sel(shamt[2]));
  Multiplexer #(.enable("false")) multiplexer_37 (
    .in0(multiplexer_19_out), .in1(multiplexer_27_out), .out(registerdest[8]), .sel(shamt[2]));
  Multiplexer #(.enable("false")) multiplexer_38 (
    .in0(multiplexer_20_out), .in1(multiplexer_28_out), .out(registerdest[9]), .sel(shamt[2]));
  Multiplexer #(.enable("false")) multiplexer_39 (
    .in0(multiplexer_21_out), .in1(multiplexer_29_out), .out(registerdest[10]), .sel(shamt[2]));
  Multiplexer #(.enable("false")) multiplexer_40 (
    .in0(multiplexer_22_out), .in1(multiplexer_30_out), .out(registerdest[11]), .sel(shamt[2]));
  Multiplexer #(.enable("false")) multiplexer_41 (
    .in0(multiplexer_25_out), .in1(1'b0), .out(registerdest[2]), .sel(shamt[2]));
  Multiplexer #(.enable("false")) multiplexer_42 (
    .in0(multiplexer_27_out), .in1(multiplexer_31_out), .out(registerdest[4]), .sel(shamt[2]));
  Multiplexer #(.enable("false")) multiplexer_43 (
    .in0(multiplexer_28_out), .in1(multiplexer_32_out), .out(registerdest[5]), .sel(shamt[2]));
  Multiplexer #(.enable("false")) multiplexer_44 (
    .in0(multiplexer_29_out), .in1(multiplexer_25_out), .out(registerdest[6]), .sel(shamt[2]));
  Multiplexer #(.enable("false")) multiplexer_45 (
    .in0(multiplexer_30_out), .in1(multiplexer_26_out), .out(registerdest[7]), .sel(shamt[2]));
  Multiplexer #(.enable("false")) multiplexer_46 (
    .in0(multiplexer_32_out), .in1(1'b0), .out(registerdest[1]), .sel(shamt[2]));
  Multiplexer #(.enable("false")) multiplexer_47 (
    .in0(multiplexer_26_out), .in1(1'b0), .out(registerdest[3]), .sel(shamt[2]));
  Multiplexer #(.enable("false")) multiplexer_48 (
    .in0(multiplexer_31_out), .in1(1'b0), .out(registerdest[0]), .sel(shamt[2]));

  // Other names for the same wires on the sheet: c1 = registerdest[0]; c2 = registerdest[1]; c3 = registerdest[2];
  //   c4 = registerdest[3]; c5 = registerdest[4]; c6 = registerdest[5]; c7 = registerdest[6]; c8 = registerdest[7];
  //   c9 = registerdest[8]; c10 = registerdest[9]; c11 = registerdest[10]; c12 = registerdest[11];
  //   c13 = registerdest[12]; c14 = registerdest[13]; c15 = registerdest[14]; c16 = registerdest[15];
  //   a1 = registersource1[0]; a2 = registersource1[1]; a3 = registersource1[2]; a4 = registersource1[3];
  //   a5 = registersource1[4]; a6 = registersource1[5]; a7 = registersource1[6]; a8 = registersource1[7];
  //   a9 = registersource1[8]; a10 = registersource1[9]; a11 = registersource1[10]; a12 = registersource1[11];
  //   a13 = registersource1[12]; a14 = registersource1[13]; a15 = registersource1[14]; a16 = registersource1[15];
  //   s1 = shamt[0]; s2 = shamt[1]; s3 = shamt[2]
endmodule

module shra (
  input  [2:0] shamt,
  input  [15:0] registersource1,
  output [15:0] registerdest
);

  wire multiplexer_1_out, multiplexer_2_out, multiplexer_3_out, multiplexer_4_out, multiplexer_5_out,
       multiplexer_6_out, multiplexer_7_out, multiplexer_8_out, multiplexer_9_out, multiplexer_10_out,
       multiplexer_11_out, multiplexer_12_out, multiplexer_13_out, multiplexer_14_out, multiplexer_15_out,
       multiplexer_16_out, multiplexer_17_out, multiplexer_18_out, multiplexer_19_out, multiplexer_20_out,
       multiplexer_21_out, multiplexer_22_out, multiplexer_23_out, multiplexer_24_out, multiplexer_25_out,
       multiplexer_26_out, multiplexer_27_out, multiplexer_28_out, multiplexer_29_out, multiplexer_30_out,
       multiplexer_31_out, multiplexer_32_out;

  Multiplexer #(.enable("false")) multiplexer_1 (
    .in0(registersource1[0]), .in1(registersource1[1]), .out(multiplexer_1_out), .sel(shamt[0]));
  Multiplexer #(.enable("false")) multiplexer_2 (
    .in0(registersource1[1]), .in1(registersource1[2]), .out(multiplexer_2_out), .sel(shamt[0]));
  Multiplexer #(.enable("false")) multiplexer_3 (
    .in0(registersource1[2]), .in1(registersource1[3]), .out(multiplexer_3_out), .sel(shamt[0]));
  Multiplexer #(.enable("false")) multiplexer_4 (
    .in0(registersource1[3]), .in1(registersource1[4]), .out(multiplexer_4_out), .sel(shamt[0]));
  Multiplexer #(.enable("false")) multiplexer_5 (
    .in0(registersource1[4]), .in1(registersource1[5]), .out(multiplexer_5_out), .sel(shamt[0]));
  Multiplexer #(.enable("false")) multiplexer_6 (
    .in0(registersource1[5]), .in1(registersource1[6]), .out(multiplexer_6_out), .sel(shamt[0]));
  Multiplexer #(.enable("false")) multiplexer_7 (
    .in0(registersource1[6]), .in1(registersource1[7]), .out(multiplexer_7_out), .sel(shamt[0]));
  Multiplexer #(.enable("false")) multiplexer_8 (
    .in0(registersource1[7]), .in1(registersource1[8]), .out(multiplexer_8_out), .sel(shamt[0]));
  Multiplexer #(.enable("false")) multiplexer_9 (
    .in0(registersource1[8]), .in1(registersource1[9]), .out(multiplexer_9_out), .sel(shamt[0]));
  Multiplexer #(.enable("false")) multiplexer_10 (
    .in0(registersource1[9]), .in1(registersource1[10]), .out(multiplexer_10_out), .sel(shamt[0]));
  Multiplexer #(.enable("false")) multiplexer_11 (
    .in0(registersource1[10]), .in1(registersource1[11]), .out(multiplexer_11_out), .sel(shamt[0]));
  Multiplexer #(.enable("false")) multiplexer_12 (
    .in0(registersource1[11]), .in1(registersource1[12]), .out(multiplexer_12_out), .sel(shamt[0]));
  Multiplexer #(.enable("false")) multiplexer_13 (
    .in0(registersource1[12]), .in1(registersource1[13]), .out(multiplexer_13_out), .sel(shamt[0]));
  Multiplexer #(.enable("false")) multiplexer_14 (
    .in0(registersource1[13]), .in1(registersource1[14]), .out(multiplexer_14_out), .sel(shamt[0]));
  Multiplexer #(.enable("false")) multiplexer_15 (
    .in0(registersource1[14]), .in1(registersource1[15]), .out(multiplexer_15_out), .sel(shamt[0]));
  Multiplexer #(.enable("false")) multiplexer_16 (
    .in0(registersource1[15]), .in1(registersource1[15]), .out(multiplexer_16_out), .sel(shamt[0]));
  Multiplexer #(.enable("false")) multiplexer_17 (
    .in0(multiplexer_1_out), .in1(multiplexer_3_out), .out(multiplexer_17_out), .sel(shamt[1]));
  Multiplexer #(.enable("false")) multiplexer_18 (
    .in0(multiplexer_2_out), .in1(multiplexer_4_out), .out(multiplexer_18_out), .sel(shamt[1]));
  Multiplexer #(.enable("false")) multiplexer_19 (
    .in0(multiplexer_3_out), .in1(multiplexer_5_out), .out(multiplexer_19_out), .sel(shamt[1]));
  Multiplexer #(.enable("false")) multiplexer_20 (
    .in0(multiplexer_4_out), .in1(multiplexer_6_out), .out(multiplexer_20_out), .sel(shamt[1]));
  Multiplexer #(.enable("false")) multiplexer_21 (
    .in0(multiplexer_5_out), .in1(multiplexer_7_out), .out(multiplexer_21_out), .sel(shamt[1]));
  Multiplexer #(.enable("false")) multiplexer_22 (
    .in0(multiplexer_6_out), .in1(multiplexer_8_out), .out(multiplexer_22_out), .sel(shamt[1]));
  Multiplexer #(.enable("false")) multiplexer_23 (
    .in0(multiplexer_7_out), .in1(multiplexer_9_out), .out(multiplexer_23_out), .sel(shamt[1]));
  Multiplexer #(.enable("false")) multiplexer_24 (
    .in0(multiplexer_8_out), .in1(multiplexer_10_out), .out(multiplexer_24_out), .sel(shamt[1]));
  Multiplexer #(.enable("false")) multiplexer_25 (
    .in0(multiplexer_9_out), .in1(multiplexer_11_out), .out(multiplexer_25_out), .sel(shamt[1]));
  Multiplexer #(.enable("false")) multiplexer_26 (
    .in0(multiplexer_10_out), .in1(multiplexer_12_out), .out(multiplexer_26_out), .sel(shamt[1]));
  Multiplexer #(.enable("false")) multiplexer_27 (
    .in0(multiplexer_11_out), .in1(multiplexer_13_out), .out(multiplexer_27_out), .sel(shamt[1]));
  Multiplexer #(.enable("false")) multiplexer_28 (
    .in0(multiplexer_12_out), .in1(multiplexer_14_out), .out(multiplexer_28_out), .sel(shamt[1]));
  Multiplexer #(.enable("false")) multiplexer_29 (
    .in0(multiplexer_13_out), .in1(multiplexer_15_out), .out(multiplexer_29_out), .sel(shamt[1]));
  Multiplexer #(.enable("false")) multiplexer_30 (
    .in0(multiplexer_14_out), .in1(multiplexer_16_out), .out(multiplexer_30_out), .sel(shamt[1]));
  Multiplexer #(.enable("false")) multiplexer_31 (
    .in0(multiplexer_16_out), .in1(registersource1[15]), .out(multiplexer_31_out), .sel(shamt[1]));
  Multiplexer #(.enable("false")) multiplexer_32 (
    .in0(multiplexer_15_out), .in1(registersource1[15]), .out(multiplexer_32_out), .sel(shamt[1]));
  Multiplexer #(.enable("false")) multiplexer_33 (
    .in0(multiplexer_18_out), .in1(multiplexer_22_out), .out(registerdest[1]), .sel(shamt[2]));
  Multiplexer #(.enable("false")) multiplexer_34 (
    .in0(multiplexer_19_out), .in1(multiplexer_23_out), .out(registerdest[2]), .sel(shamt[2]));
  Multiplexer #(.enable("false")) multiplexer_35 (
    .in0(multiplexer_17_out), .in1(multiplexer_21_out), .out(registerdest[0]), .sel(shamt[2]));
  Multiplexer #(.enable("false")) multiplexer_36 (
    .in0(multiplexer_20_out), .in1(multiplexer_24_out), .out(registerdest[3]), .sel(shamt[2]));
  Multiplexer #(.enable("false")) multiplexer_37 (
    .in0(multiplexer_21_out), .in1(multiplexer_25_out), .out(registerdest[4]), .sel(shamt[2]));
  Multiplexer #(.enable("false")) multiplexer_38 (
    .in0(multiplexer_22_out), .in1(multiplexer_26_out), .out(registerdest[5]), .sel(shamt[2]));
  Multiplexer #(.enable("false")) multiplexer_39 (
    .in0(multiplexer_23_out), .in1(multiplexer_27_out), .out(registerdest[6]), .sel(shamt[2]));
  Multiplexer #(.enable("false")) multiplexer_40 (
    .in0(multiplexer_24_out), .in1(multiplexer_28_out), .out(registerdest[7]), .sel(shamt[2]));
  Multiplexer #(.enable("false")) multiplexer_41 (
    .in0(multiplexer_25_out), .in1(multiplexer_29_out), .out(registerdest[8]), .sel(shamt[2]));
  Multiplexer #(.enable("false")) multiplexer_42 (
    .in0(multiplexer_26_out), .in1(multiplexer_30_out), .out(registerdest[9]), .sel(shamt[2]));
  Multiplexer #(.enable("false")) multiplexer_43 (
    .in0(multiplexer_27_out), .in1(multiplexer_32_out), .out(registerdest[10]), .sel(shamt[2]));
  Multiplexer #(.enable("false")) multiplexer_44 (
    .in0(multiplexer_28_out), .in1(multiplexer_31_out), .out(registerdest[11]), .sel(shamt[2]));
  Multiplexer #(.enable("false")) multiplexer_45 (
    .in0(multiplexer_29_out), .in1(registersource1[15]), .out(registerdest[12]), .sel(shamt[2]));
  Multiplexer #(.enable("false")) multiplexer_46 (
    .in0(multiplexer_30_out), .in1(registersource1[15]), .out(registerdest[13]), .sel(shamt[2]));
  Multiplexer #(.enable("false")) multiplexer_47 (
    .in0(multiplexer_32_out), .in1(registersource1[15]), .out(registerdest[14]), .sel(shamt[2]));
  Multiplexer #(.enable("false")) multiplexer_48 (
    .in0(multiplexer_31_out), .in1(registersource1[15]), .out(registerdest[15]), .sel(shamt[2]));

  // Other names for the same wires on the sheet: c1 = registerdest[0]; c2 = registerdest[1]; c3 = registerdest[2];
  //   c4 = registerdest[3]; c5 = registerdest[4]; c6 = registerdest[5]; c7 = registerdest[6]; c8 = registerdest[7];
  //   c9 = registerdest[8]; c10 = registerdest[9]; c11 = registerdest[10]; c12 = registerdest[11];
  //   c13 = registerdest[12]; c14 = registerdest[13]; c15 = registerdest[14]; c16 = registerdest[15];
  //   a1 = registersource1[0]; a2 = registersource1[1]; a3 = registersource1[2]; a4 = registersource1[3];
  //   a5 = registersource1[4]; a6 = registersource1[5]; a7 = registersource1[6]; a8 = registersource1[7];
  //   a9 = registersource1[8]; a10 = registersource1[9]; a11 = registersource1[10]; a12 = registersource1[11];
  //   a13 = registersource1[12]; a14 = registersource1[13]; a15 = registersource1[14]; a16 = registersource1[15];
  //   s1 = shamt[0]; s2 = shamt[1]; s3 = shamt[2]
endmodule

module RegisterFile (
  input  [2:0] registerdest,
  input  [15:0] data_in,
  input  clk,
  input  reset,
  input  we_writeregister,
  input  [2:0] rs1,
  input  [2:0] rs2,
  output [15:0] rs1content,
  output [15:0] rs2content
);

  wire decoder_1_out1, decoder_1_out2, decoder_1_out3, decoder_1_out4, decoder_1_out5, decoder_1_out6,
       decoder_1_out7, decoder_2_out0, decoder_2_out1, decoder_2_out2, decoder_2_out3, decoder_2_out4,
       decoder_2_out5, decoder_2_out6, decoder_2_out7, decoder_3_out0, decoder_3_out1, decoder_3_out2,
       decoder_3_out3, decoder_3_out4, decoder_3_out5, decoder_3_out6, decoder_3_out7;
  wire [15:0] reg_1_data_out, reg_2_data_out, reg_3_data_out, reg_4_data_out, reg_5_data_out, reg_6_data_out,
       reg_7_data_out;

  Decoder #(.select(3)) decoder_1 (
    .out1(decoder_1_out1), .out2(decoder_1_out2), .out3(decoder_1_out3), .out4(decoder_1_out4),
    .out5(decoder_1_out5), .out6(decoder_1_out6), .out7(decoder_1_out7), .sel(registerdest),
    .en(we_writeregister));  // open: out0
  // Probe on reg_1_data_out
  \reg  reg_1 (.data_in(data_in), .clk(clk), .we(decoder_1_out1), .reset(reset), .data_out(reg_1_data_out));
  // Probe on reg_2_data_out
  \reg  reg_2 (.data_in(data_in), .clk(clk), .we(decoder_1_out2), .reset(reset), .data_out(reg_2_data_out));
  // Probe on reg_3_data_out
  \reg  reg_3 (.data_in(data_in), .clk(clk), .we(decoder_1_out3), .reset(reset), .data_out(reg_3_data_out));
  // Probe on reg_4_data_out
  \reg  reg_4 (.data_in(data_in), .clk(clk), .we(decoder_1_out4), .reset(reset), .data_out(reg_4_data_out));
  // Probe on reg_5_data_out
  \reg  reg_5 (.data_in(data_in), .clk(clk), .we(decoder_1_out5), .reset(reset), .data_out(reg_5_data_out));
  // Probe on reg_6_data_out
  \reg  reg_6 (.data_in(data_in), .clk(clk), .we(decoder_1_out6), .reset(reset), .data_out(reg_6_data_out));
  // Probe on reg_7_data_out
  \reg  reg_7 (.data_in(data_in), .clk(clk), .we(decoder_1_out7), .reset(reset), .data_out(reg_7_data_out));
  Decoder #(.select(3)) decoder_2 (
    .out0(decoder_2_out0), .out1(decoder_2_out1), .out2(decoder_2_out2), .out3(decoder_2_out3),
    .out4(decoder_2_out4), .out5(decoder_2_out5), .out6(decoder_2_out6), .out7(decoder_2_out7), .sel(rs1));  // open: en
  // Probe on {16{1'b0}}
  assign rs1content = decoder_2_out0 ? {16{1'b0}} : 16'bz;  // Controlled_Buffer controlled_buffer_1
  assign rs1content = decoder_2_out1 ? reg_1_data_out : 16'bz;  // Controlled_Buffer controlled_buffer_2
  assign rs1content = decoder_2_out2 ? reg_2_data_out : 16'bz;  // Controlled_Buffer controlled_buffer_3
  assign rs1content = decoder_2_out3 ? reg_3_data_out : 16'bz;  // Controlled_Buffer controlled_buffer_4
  assign rs1content = decoder_2_out4 ? reg_4_data_out : 16'bz;  // Controlled_Buffer controlled_buffer_5
  assign rs1content = decoder_2_out5 ? reg_5_data_out : 16'bz;  // Controlled_Buffer controlled_buffer_6
  assign rs1content = decoder_2_out6 ? reg_6_data_out : 16'bz;  // Controlled_Buffer controlled_buffer_7
  assign rs1content = decoder_2_out7 ? reg_7_data_out : 16'bz;  // Controlled_Buffer controlled_buffer_8
  Decoder #(.select(3)) decoder_3 (
    .out0(decoder_3_out0), .out1(decoder_3_out1), .out2(decoder_3_out2), .out3(decoder_3_out3),
    .out4(decoder_3_out4), .out5(decoder_3_out5), .out6(decoder_3_out6), .out7(decoder_3_out7), .sel(rs2));  // open: en
  assign rs2content = decoder_3_out0 ? {16{1'b0}} : 16'bz;  // Controlled_Buffer controlled_buffer_9
  assign rs2content = decoder_3_out1 ? reg_1_data_out : 16'bz;  // Controlled_Buffer controlled_buffer_10
  assign rs2content = decoder_3_out2 ? reg_2_data_out : 16'bz;  // Controlled_Buffer controlled_buffer_11
  assign rs2content = decoder_3_out3 ? reg_3_data_out : 16'bz;  // Controlled_Buffer controlled_buffer_12
  assign rs2content = decoder_3_out4 ? reg_4_data_out : 16'bz;  // Controlled_Buffer controlled_buffer_13
  assign rs2content = decoder_3_out5 ? reg_5_data_out : 16'bz;  // Controlled_Buffer controlled_buffer_14
  assign rs2content = decoder_3_out6 ? reg_6_data_out : 16'bz;  // Controlled_Buffer controlled_buffer_15
  assign rs2content = decoder_3_out7 ? reg_7_data_out : 16'bz;  // Controlled_Buffer controlled_buffer_16
endmodule

module \reg  (
  input  [15:0] data_in,
  input  clk,
  input  we,
  input  reset,
  output [15:0] data_out
);

  wire and_1_out;

  and and_1 (and_1_out, clk, we);
  D_Flip_Flop d_ff_1 (.D(data_in[0]), .clk(and_1_out), .Q(data_out[0]), .reset(reset));  // open: Qn, preset
  D_Flip_Flop d_ff_2 (.D(data_in[1]), .clk(and_1_out), .Q(data_out[1]), .reset(reset));  // open: Qn, preset
  D_Flip_Flop d_ff_3 (.D(data_in[2]), .clk(and_1_out), .Q(data_out[2]), .reset(reset));  // open: Qn, preset
  D_Flip_Flop d_ff_4 (.D(data_in[3]), .clk(and_1_out), .Q(data_out[3]), .reset(reset));  // open: Qn, preset
  D_Flip_Flop d_ff_5 (.D(data_in[4]), .clk(and_1_out), .Q(data_out[4]), .reset(reset));  // open: Qn, preset
  D_Flip_Flop d_ff_6 (.D(data_in[5]), .clk(and_1_out), .Q(data_out[5]), .reset(reset));  // open: Qn, preset
  D_Flip_Flop d_ff_7 (.D(data_in[6]), .clk(and_1_out), .Q(data_out[6]), .reset(reset));  // open: Qn, preset
  D_Flip_Flop d_ff_8 (.D(data_in[7]), .clk(and_1_out), .Q(data_out[7]), .reset(reset));  // open: Qn, preset
  D_Flip_Flop d_ff_9 (.D(data_in[8]), .clk(and_1_out), .Q(data_out[8]), .reset(reset));  // open: Qn, preset
  D_Flip_Flop d_ff_10 (.D(data_in[9]), .clk(and_1_out), .Q(data_out[9]), .reset(reset));  // open: Qn, preset
  D_Flip_Flop d_ff_11 (.D(data_in[10]), .clk(and_1_out), .Q(data_out[10]), .reset(reset));  // open: Qn, preset
  D_Flip_Flop d_ff_12 (.D(data_in[11]), .clk(and_1_out), .Q(data_out[11]), .reset(reset));  // open: Qn, preset
  D_Flip_Flop d_ff_13 (.D(data_in[12]), .clk(and_1_out), .Q(data_out[12]), .reset(reset));  // open: Qn, preset
  D_Flip_Flop d_ff_14 (.D(data_in[13]), .clk(and_1_out), .Q(data_out[13]), .reset(reset));  // open: Qn, preset
  D_Flip_Flop d_ff_15 (.D(data_in[14]), .clk(and_1_out), .Q(data_out[14]), .reset(reset));  // open: Qn, preset
  D_Flip_Flop d_ff_16 (.D(data_in[15]), .clk(and_1_out), .Q(data_out[15]), .reset(reset));  // open: Qn, preset

  // Other names for the same wires on the sheet: rst = reset
endmodule

module memorysubcircuit (
  input  [15:0] address,
  input  WE,
  input  clk,
  input  [15:0] data_in,
  output [15:0] address_latched,
  output WE_latched,
  output OE_latched,
  output [15:0] data_in_latched
);

  wire d_ff_1_q;
  wire [15:0] register_1_q;

  Register #(.width(16), .trigger("falling")) register_1 (
    .D(address), .en(WE), .clk(clk), .Q(register_1_q));  // open: clr
  D_Flip_Flop #(.trigger("falling")) d_ff_1 (.D(WE), .clk(clk), .Q(d_ff_1_q));  // open: Qn, preset, reset
  Register #(.width(16), .trigger("falling")) register_2 (
    .D(data_in), .en(WE), .clk(clk), .Q(data_in_latched));  // open: clr
  Multiplexer #(.width(16), .enable("false")) multiplexer_1 (
    .in0(address), .in1(register_1_q), .out(address_latched), .sel(d_ff_1_q));
  and and_1 (WE_latched, clk, d_ff_1_q);
  not not_1 (OE_latched, WE_latched);
endmodule

module ALUcontrol (
  input  [3:0] opcode,
  output [2:0] ALUop
);

  wire and_1_out, and_2_out, and_3_out, and_4_out, and_6_out, and_7_out, and_8_out, and_9_out, and_10_out,
       and_11_out, and_12_out, and_13_out, not_1_out, not_2_out, not_3_out, not_4_out, not_5_out, not_6_out,
       not_7_out, not_8_out, not_9_out, not_10_out, not_11_out, not_12_out, not_13_out, not_14_out,
       not_15_out;

  not not_1 (not_1_out, opcode[0]);
  not not_2 (not_2_out, opcode[1]);
  not not_3 (not_3_out, opcode[2]);
  not not_4 (not_4_out, opcode[3]);
  and and_1 (and_1_out, opcode[0], opcode[1], opcode[2], not_4_out);
  not not_5 (not_5_out, and_1_out);
  and and_2 (and_2_out, not_1_out, opcode[1], not_3_out, opcode[3]);
  and and_3 (and_3_out, opcode[0], opcode[1], not_3_out, opcode[3]);
  and and_4 (and_4_out, not_1_out, opcode[1], opcode[2], not_4_out);
  assign ALUop = and_1_out ? 3'b001 : 3'bz;  // Controlled_Buffer and_5
  assign ALUop = and_6_out ? 3'b010 : 3'bz;  // Controlled_Buffer add
  and and_6 (and_6_out, opcode[0], not_2_out, not_3_out, opcode[3]);
  not not_6 (not_6_out, and_2_out);
  not not_7 (not_7_out, and_3_out);
  not not_8 (not_8_out, and_7_out);
  and and_7 (and_7_out, not_1_out, not_2_out, opcode[2], opcode[3]);
  not not_9 (not_9_out, and_8_out);
  and and_8 (and_8_out, not_1_out, not_2_out, opcode[2], not_4_out);
  and and_9 (and_9_out, opcode[0], not_2_out, opcode[2], not_4_out);
  assign ALUop = and_4_out ? 3'b000 : 3'bz;  // Controlled_Buffer or
  and and_10 (and_10_out, not_1_out, not_2_out, not_3_out, opcode[3]);
  assign ALUop = and_2_out ? 3'b011 : 3'bz;  // Controlled_Buffer sub
  not not_10 (not_10_out, and_4_out);
  not not_11 (not_11_out, and_6_out);
  and and_11 (and_11_out, not_10_out, not_14_out, not_5_out, not_11_out, not_6_out, not_7_out, not_8_out, not_9_out, not_13_out, not_12_out, not_15_out);
  not not_12 (not_12_out, and_12_out);
  not not_13 (not_13_out, and_9_out);
  assign ALUop = and_8_out ? 3'b011 : 3'bz;  // Controlled_Buffer beq
  assign ALUop = and_9_out ? 3'b011 : 3'bz;  // Controlled_Buffer bgt
  assign ALUop = and_10_out ? 3'b010 : 3'bz;  // Controlled_Buffer addi
  not not_14 (not_14_out, and_10_out);
  assign ALUop = and_11_out ? 3'b110 : 3'bz;  // Controlled_Buffer controlled_buffer_1
  assign ALUop = and_3_out ? 3'b100 : 3'bz;  // Controlled_Buffer shra
  assign ALUop = and_7_out ? 3'b101 : 3'bz;  // Controlled_Buffer shl
  assign ALUop = and_12_out ? 3'b010 : 3'bz;  // Controlled_Buffer lw
  and and_12 (and_12_out, not_1_out, opcode[1], not_3_out, not_4_out);
  not not_15 (not_15_out, and_13_out);
  assign ALUop = and_13_out ? 3'b010 : 3'bz;  // Controlled_Buffer sw
  and and_13 (and_13_out, opcode[0], opcode[1], not_3_out, not_4_out);
endmodule

module signextender (
  input  [5:0] imm,
  output [15:0] newimm
);


  assign newimm = {{11{imm[5]}}, imm[4:0]};
endmodule

module selectors (
  input  [3:0] opcode,
  output [1:0] ALUorDMorinputorNextPC,
  output jal,
  output jr,
  output j,
  output ALUinB,
  output beq,
  output rdrs2,
  output bgt,
  output memory,
  output rwe
);

  wire add_out, addi_out, and_2_out, and_out, input_out, lw_out, not_1_out, not_2_out, not_3_out, not_4_out,
       not_5_out, not_6_out, not_7_out, or_out, shl_out, shra_out, sub_out, sw_out;

  not not_1 (not_1_out, opcode[0]);
  not not_2 (not_2_out, opcode[3]);
  and add (add_out, opcode[0], not_3_out, not_4_out, opcode[3]);
  and sub (sub_out, not_1_out, opcode[1], not_4_out, opcode[3]);
  and shra (shra_out, opcode[0], opcode[1], not_4_out, opcode[3]);
  not not_3 (not_3_out, opcode[1]);
  and \and  (and_out, opcode[0], opcode[1], opcode[2], not_2_out);
  and \or  (or_out, not_1_out, opcode[1], opcode[2], not_2_out);
  not not_4 (not_4_out, opcode[2]);
  and lw (lw_out, not_1_out, opcode[1], not_4_out, not_2_out);
  and u_beq (beq, not_1_out, not_3_out, opcode[2], not_2_out);
  and addi (addi_out, not_1_out, not_3_out, not_4_out, opcode[3]);
  assign ALUorDMorinputorNextPC = lw_out ? 2'b01 : 2'bz;  // Controlled_Buffer controlled_buffer_1
  and sw (sw_out, opcode[0], opcode[1], not_4_out, not_2_out);
  and u_bgt (bgt, opcode[0], not_3_out, opcode[2], not_2_out);
  and shl (shl_out, not_1_out, not_3_out, opcode[2], opcode[3]);
  not not_5 (not_5_out, lw_out);
  not not_6 (not_6_out, input_out);
  assign ALUorDMorinputorNextPC = input_out ? 2'b10 : 2'bz;  // Controlled_Buffer controlled_buffer_2
  and \input  (input_out, opcode[0], not_3_out, not_4_out, not_2_out);
  and and_2 (and_2_out, not_5_out, not_7_out, not_6_out);
  or or_2 (ALUinB, lw_out, sw_out, addi_out);
  not not_7 (not_7_out, jal);
  assign ALUorDMorinputorNextPC = and_2_out ? 2'b00 : 2'bz;  // Controlled_Buffer controlled_buffer_3
  assign ALUorDMorinputorNextPC = jal ? 2'b11 : 2'bz;  // Controlled_Buffer controlled_buffer_4
  and u_jal (jal, not_1_out, opcode[1], opcode[2], opcode[3]);
  and u_jr (jr, opcode[0], opcode[1], opcode[2], opcode[3]);
  and u_j (j, opcode[0], not_3_out, opcode[2], opcode[3]);
  or or_3 (memory, lw_out, sw_out);
  or or_4 (rwe, addi_out, input_out, lw_out, or_out, and_out, add_out, sub_out, shra_out, shl_out, jal);

  assign rdrs2 = ALUinB;
endmodule
